// Logisim project Shadow-Core.circ as structural Verilog: 12 circuits, main circuit Register File
module Register_File (
  input  Reg_Write,
  input  [31:0] Data,
  input  [4:0] rs1,
  input  [4:0] rs2,
  input  [4:0] rd,
  input  Clock,
  input  Reset,
  output [31:0] Read_01,
  output [31:0] Read_02
);

  wire and_1_out, and_2_out, and_3_out, and_4_out, and_5_out, and_6_out, and_7_out, and_8_out, and_9_out,
       and_10_out, and_11_out, and_12_out, and_13_out, and_14_out, and_15_out, and_16_out, and_17_out,
       and_18_out, and_19_out, and_20_out, and_21_out, and_22_out, and_23_out, and_24_out, and_25_out,
       and_26_out, and_27_out, and_28_out, and_29_out, and_30_out, and_31_out, and_32_out, decoder_1_out1,
       decoder_1_out2, decoder_1_out3, decoder_1_out4, decoder_1_out5, decoder_1_out6, decoder_1_out7,
       decoder_1_out8, decoder_1_out9, decoder_1_out10, decoder_1_out11, decoder_1_out12, decoder_1_out13,
       decoder_1_out14, decoder_1_out15, decoder_1_out16, decoder_1_out17, decoder_1_out18, decoder_1_out19,
       decoder_1_out20, decoder_1_out21, decoder_1_out22, decoder_1_out23, decoder_1_out24, decoder_1_out25,
       decoder_1_out26, decoder_1_out27, decoder_1_out28, decoder_1_out29, decoder_1_out30, decoder_1_out31;
  wire [31:0] x0_q, x1_q, x2_q, x3_q, x4_q, x5_q, x6_q, x7_q, x8_q, x9_q, x10_q, x11_q, x12_q, x13_q, x14_q,
       x15_q, x16_q, x17_q, x18_q, x19_q, x20_q, x21_q, x22_q, x23_q, x24_q, x25_q, x26_q, x27_q, x28_q,
       x29_q, x30_q, x31_q;

  Decoder #(.select(5)) decoder_1 (
    .out1(decoder_1_out1), .out2(decoder_1_out2), .out3(decoder_1_out3), .out4(decoder_1_out4),
    .out5(decoder_1_out5), .out6(decoder_1_out6), .out7(decoder_1_out7), .out8(decoder_1_out8),
    .out9(decoder_1_out9), .out10(decoder_1_out10), .out11(decoder_1_out11), .out12(decoder_1_out12),
    .out13(decoder_1_out13), .out14(decoder_1_out14), .out15(decoder_1_out15), .out16(decoder_1_out16),
    .out17(decoder_1_out17), .out18(decoder_1_out18), .out19(decoder_1_out19), .out20(decoder_1_out20),
    .out21(decoder_1_out21), .out22(decoder_1_out22), .out23(decoder_1_out23), .out24(decoder_1_out24),
    .out25(decoder_1_out25), .out26(decoder_1_out26), .out27(decoder_1_out27), .out28(decoder_1_out28),
    .out29(decoder_1_out29), .out30(decoder_1_out30), .out31(decoder_1_out31), .sel(rd), .en(1'b1));  // open: out0
  and and_1 (and_1_out, Reg_Write, 1'b0);
  and and_2 (and_2_out, Reg_Write, decoder_1_out1);
  and and_3 (and_3_out, Reg_Write, decoder_1_out2);
  and and_4 (and_4_out, Reg_Write, decoder_1_out3);
  and and_5 (and_5_out, Reg_Write, decoder_1_out4);
  and and_6 (and_6_out, Reg_Write, decoder_1_out5);
  and and_7 (and_7_out, Reg_Write, decoder_1_out6);
  and and_8 (and_8_out, Reg_Write, decoder_1_out7);
  Register #(.width(32)) x0 (.D(Data), .en(and_1_out), .Q(x0_q), .clk(Clock), .clr(Reset));
  Register #(.width(32)) x1 (.D(Data), .en(and_2_out), .Q(x1_q), .clk(Clock), .clr(Reset));
  Register #(.width(32)) x2 (.D(Data), .en(and_3_out), .Q(x2_q), .clk(Clock), .clr(Reset));
  Register #(.width(32)) x3 (.D(Data), .en(and_4_out), .Q(x3_q), .clk(Clock), .clr(Reset));
  Register #(.width(32)) x4 (.D(Data), .en(and_5_out), .Q(x4_q), .clk(Clock), .clr(Reset));
  Register #(.width(32)) x5 (.D(Data), .en(and_6_out), .Q(x5_q), .clk(Clock), .clr(Reset));
  Register #(.width(32)) x6 (.D(Data), .en(and_7_out), .Q(x6_q), .clk(Clock), .clr(Reset));
  Register #(.width(32)) x7 (.D(Data), .en(and_8_out), .Q(x7_q), .clk(Clock), .clr(Reset));
  and and_9 (and_9_out, Reg_Write, decoder_1_out8);
  Register #(.width(32)) x8 (.D(Data), .en(and_9_out), .Q(x8_q), .clk(Clock), .clr(Reset));
  and and_10 (and_10_out, Reg_Write, decoder_1_out9);
  Register #(.width(32)) x9 (.D(Data), .en(and_10_out), .Q(x9_q), .clk(Clock), .clr(Reset));
  Register #(.width(32)) x10 (.D(Data), .en(and_11_out), .Q(x10_q), .clk(Clock), .clr(Reset));
  and and_11 (and_11_out, Reg_Write, decoder_1_out10);
  and and_12 (and_12_out, Reg_Write, decoder_1_out11);
  Register #(.width(32)) x11 (.D(Data), .en(and_12_out), .Q(x11_q), .clk(Clock), .clr(Reset));
  and and_13 (and_13_out, Reg_Write, decoder_1_out12);
  Register #(.width(32)) x12 (.D(Data), .en(and_13_out), .Q(x12_q), .clk(Clock), .clr(Reset));
  and and_14 (and_14_out, Reg_Write, decoder_1_out13);
  Register #(.width(32)) x13 (.D(Data), .en(and_14_out), .Q(x13_q), .clk(Clock), .clr(Reset));
  and and_15 (and_15_out, Reg_Write, decoder_1_out14);
  Register #(.width(32)) x14 (.D(Data), .en(and_15_out), .Q(x14_q), .clk(Clock), .clr(Reset));
  Register #(.width(32)) x15 (.D(Data), .en(and_16_out), .Q(x15_q), .clk(Clock), .clr(Reset));
  and and_16 (and_16_out, Reg_Write, decoder_1_out15);
  and and_17 (and_17_out, Reg_Write, decoder_1_out16);
  and and_18 (and_18_out, Reg_Write, decoder_1_out17);
  and and_19 (and_19_out, Reg_Write, decoder_1_out18);
  and and_20 (and_20_out, Reg_Write, decoder_1_out19);
  and and_21 (and_21_out, Reg_Write, decoder_1_out20);
  and and_22 (and_22_out, Reg_Write, decoder_1_out21);
  and and_23 (and_23_out, Reg_Write, decoder_1_out22);
  and and_24 (and_24_out, Reg_Write, decoder_1_out23);
  Register #(.width(32)) x16 (.D(Data), .en(and_17_out), .Q(x16_q), .clk(Clock), .clr(Reset));
  Register #(.width(32)) x17 (.D(Data), .en(and_18_out), .Q(x17_q), .clk(Clock), .clr(Reset));
  Register #(.width(32)) x18 (.D(Data), .en(and_19_out), .Q(x18_q), .clk(Clock), .clr(Reset));
  Register #(.width(32)) x19 (.D(Data), .en(and_20_out), .Q(x19_q), .clk(Clock), .clr(Reset));
  Register #(.width(32)) x20 (.D(Data), .en(and_21_out), .Q(x20_q), .clk(Clock), .clr(Reset));
  Register #(.width(32)) x21 (.D(Data), .en(and_22_out), .Q(x21_q), .clk(Clock), .clr(Reset));
  Register #(.width(32)) x22 (.D(Data), .en(and_23_out), .Q(x22_q), .clk(Clock), .clr(Reset));
  Register #(.width(32)) x23 (.D(Data), .en(and_24_out), .Q(x23_q), .clk(Clock), .clr(Reset));
  and and_25 (and_25_out, Reg_Write, decoder_1_out24);
  Register #(.width(32)) x24 (.D(Data), .en(and_25_out), .Q(x24_q), .clk(Clock), .clr(Reset));
  Register #(.width(32)) x25 (.D(Data), .en(and_26_out), .Q(x25_q), .clk(Clock), .clr(Reset));
  and and_26 (and_26_out, Reg_Write, decoder_1_out25);
  and and_27 (and_27_out, Reg_Write, decoder_1_out26);
  Register #(.width(32)) x26 (.D(Data), .en(and_27_out), .Q(x26_q), .clk(Clock), .clr(Reset));
  and and_28 (and_28_out, Reg_Write, decoder_1_out27);
  Register #(.width(32)) x27 (.D(Data), .en(and_28_out), .Q(x27_q), .clk(Clock), .clr(Reset));
  and and_29 (and_29_out, Reg_Write, decoder_1_out28);
  Register #(.width(32)) x28 (.D(Data), .en(and_29_out), .Q(x28_q), .clk(Clock), .clr(Reset));
  and and_30 (and_30_out, Reg_Write, decoder_1_out29);
  Register #(.width(32)) x29 (.D(Data), .en(and_30_out), .Q(x29_q), .clk(Clock), .clr(Reset));
  Register #(.width(32)) x30 (.D(Data), .en(and_31_out), .Q(x30_q), .clk(Clock), .clr(Reset));
  and and_31 (and_31_out, Reg_Write, decoder_1_out30);
  and and_32 (and_32_out, Reg_Write, decoder_1_out31);
  Register #(.width(32)) x31 (.D(Data), .en(and_32_out), .Q(x31_q), .clk(Clock), .clr(Reset));
  Multiplexer #(.select(5), .width(32), .enable("false")) multiplexer_1 (
    .in0(x0_q), .in1(x1_q), .in2(x2_q), .in3(x3_q), .in4(x4_q), .in5(x5_q), .in6(x6_q), .in7(x7_q),
    .in8(x8_q), .in9(x9_q), .in10(x10_q), .in11(x11_q), .in12(x12_q), .in13(x13_q), .in14(x14_q),
    .in15(x15_q), .in16(x16_q), .in17(x17_q), .in18(x18_q), .in19(x19_q), .in20(x20_q), .in21(x21_q),
    .in22(x22_q), .in23(x23_q), .in24(x24_q), .in25(x25_q), .in26(x26_q), .in27(x27_q), .in28(x28_q),
    .in29(x29_q), .in30(x30_q), .in31(x31_q), .out(Read_01), .sel(rs1));
  Multiplexer #(.select(5), .width(32), .enable("false")) multiplexer_2 (
    .in0(x0_q), .in1(x1_q), .in2(x2_q), .in3(x3_q), .in4(x4_q), .in5(x5_q), .in6(x6_q), .in7(x7_q),
    .in8(x8_q), .in9(x9_q), .in10(x10_q), .in11(x11_q), .in12(x12_q), .in13(x13_q), .in14(x14_q),
    .in15(x15_q), .in16(x16_q), .in17(x17_q), .in18(x18_q), .in19(x19_q), .in20(x20_q), .in21(x21_q),
    .in22(x22_q), .in23(x23_q), .in24(x24_q), .in25(x25_q), .in26(x26_q), .in27(x27_q), .in28(x28_q),
    .in29(x29_q), .in30(x30_q), .in31(x31_q), .out(Read_02), .sel(rs2));
endmodule

module Immediate_Generator (
  input  [31:0] Instruction,
  input  [31:0] PC,
  output [31:0] I_Type,
  output [31:0] S_Type,
  output [31:0] SB_Type,
  output [31:0] U_Type,
  output [31:0] UJ_Type
);

  wire [31:0] bit_extender_3_out, bit_extender_4_out, bit_extender_5_out;

  assign I_Type = {{20{Instruction[31]}}, Instruction[31:20]};  // Bit_Extender bit_extender_1
  assign S_Type = {{20{Instruction[31]}}, {Instruction[31:25], Instruction[11:7]}};  // Bit_Extender bit_extender_2
  assign bit_extender_3_out = {{19{Instruction[31]}}, {Instruction[31], Instruction[7], Instruction[30:25], Instruction[11:8], 1'b0}};  // Bit_Extender bit_extender_3
  assign bit_extender_4_out = {{12{Instruction[31]}}, Instruction[31:12]};  // Bit_Extender bit_extender_4
  assign bit_extender_5_out = {{11{Instruction[31]}}, {Instruction[31], Instruction[19:12], Instruction[20], Instruction[30:21], 1'b0}};  // Bit_Extender bit_extender_5
  Adder #(.width(32)) adder_1 (.a(bit_extender_3_out), .b(PC), .out(SB_Type));  // open: cin, cout
  Shifter #(.width(32)) shifter_1 (.in(bit_extender_4_out), .\dist (5'b01100), .out(U_Type));
  Adder #(.width(32)) adder_2 (.a(bit_extender_5_out), .b(PC), .out(UJ_Type));  // open: cin, cout
endmodule

module Main (
);

  wire alu_1_branch, and_1_out, Clock_out, controller_1_branch, controller_1_mem_read,
       controller_1_mem_to_reg, controller_1_mem_write, controller_1_operand_b, controller_1_reg_write,
       Reset_Data_Memory_out, Reset_PC_out, Reset_Register_out;
  wire [1:0] controller_1_extend_sel, controller_1_next_pc, controller_1_operand_a;
  wire [2:0] controller_1_aluop;
  wire [4:0] alucontroller_1_out_4;
  wire [31:0] adder_1_out, adder_for_jalr_1_computed_address, alu_1_output, Immediate_Extender_i_type,
       Immediate_Extender_s_type, Immediate_Extender_sb_type, Immediate_Extender_u_type,
       Immediate_Extender_uj_type, multiplexer_1_out, multiplexer_2_out, multiplexer_3_out,
       multiplexer_4_out, multiplexer_5_out, multiplexer_6_out, PC_q, ram_1_data, Register_File_read_01,
       Register_File_read_02, rom_1_data;

  Register #(.width(32)) PC (.D(multiplexer_1_out), .en(1'b1), .Q(PC_q), .clk(Clock_out), .clr(Reset_PC_out));
  Button Reset_PC (.out(Reset_PC_out));
  Clock Clock (.out(Clock_out));
  Button Reset_Register (.out(Reset_Register_out));
  Button Reset_Data_Memory (.out(Reset_Data_Memory_out));
  Adder #(.width(32)) adder_1 (.a(32'h4), .b(PC_q), .out(adder_1_out));  // open: cin, cout
  ROM #(.addrWidth(24), .dataWidth(32)) rom_1 (.addr(PC_q[25:2]), .data(rom_1_data), .sel(1'b1));
  Multiplexer #(.select(2), .width(32), .enable("false")) multiplexer_1 (
    .in0(adder_1_out), .in1(Immediate_Extender_uj_type), .in2(adder_for_jalr_1_computed_address),
    .in3(multiplexer_2_out), .out(multiplexer_1_out), .sel(controller_1_next_pc));
  Multiplexer #(.width(32), .enable("false")) multiplexer_2 (
    .in0(adder_1_out), .in1(Immediate_Extender_sb_type), .out(multiplexer_2_out), .sel(and_1_out));
  Immediate_Generator Immediate_Extender (
    .Instruction(rom_1_data), .PC(PC_q), .I_Type(Immediate_Extender_i_type),
    .S_Type(Immediate_Extender_s_type), .SB_Type(Immediate_Extender_sb_type),
    .U_Type(Immediate_Extender_u_type), .UJ_Type(Immediate_Extender_uj_type));
  and and_1 (and_1_out, alu_1_branch, controller_1_branch);
  Controller controller_1 (
    .Opcode(rom_1_data[6:0]), .ALUOP(controller_1_aluop), .Next_PC(controller_1_next_pc),
    .Operand_B(controller_1_operand_b), .Operand_A(controller_1_operand_a),
    .Extend_Sel(controller_1_extend_sel), .Branch(controller_1_branch), .Mem_To_Reg(controller_1_mem_to_reg),
    .Mem_Read(controller_1_mem_read), .Mem_Write(controller_1_mem_write), .Reg_Write(controller_1_reg_write));
  Register_File Register_File (
    .Reg_Write(controller_1_reg_write), .Data(multiplexer_6_out), .Clock(Clock_out),
    .Reset(Reset_Register_out), .Read_01(Register_File_read_01), .rs1(rom_1_data[19:15]),
    .Read_02(Register_File_read_02), .rs2(rom_1_data[24:20]), .rd(rom_1_data[11:7]));
  Adder_for_JALR adder_for_jalr_1 (
    .RS1(Register_File_read_01), .IMM(multiplexer_3_out), .Computed_Address(adder_for_jalr_1_computed_address));
  Multiplexer #(.select(2), .width(32), .enable("false")) multiplexer_3 (
    .in0(Immediate_Extender_i_type), .in1(Immediate_Extender_s_type), .in2(Immediate_Extender_u_type),
    .out(multiplexer_3_out), .sel(controller_1_extend_sel));  // open: in3
  Multiplexer #(.width(32), .enable("false")) multiplexer_4 (
    .in0(Register_File_read_02), .in1(multiplexer_3_out), .out(multiplexer_4_out),
    .sel(controller_1_operand_b));
  Multiplexer #(.select(2), .width(32), .enable("false")) multiplexer_5 (
    .in0(Register_File_read_01), .in1(PC_q), .in2(adder_1_out), .in3(Register_File_read_01),
    .out(multiplexer_5_out), .sel(controller_1_operand_a));
  ALU alu_1 (
    .Operand_A(multiplexer_5_out), .Operand_B(multiplexer_4_out), .Output(alu_1_output),
    .Branch(alu_1_branch), .ALUOperation(alucontroller_1_out_4));
  ALUController alucontroller_1 (
    .out_4(alucontroller_1_out_4), .ALUOP(controller_1_aluop), .f7(rom_1_data[30]), .f3(rom_1_data[14:12]));
  RAM #(.addrWidth(24), .dataWidth(32), .bus("separate")) ram_1 (
    .addr(alu_1_output[25:2]), .din(Register_File_read_02), .data(ram_1_data), .str(controller_1_mem_write),
    .sel(1'b1), .clk(Clock_out), .ld(controller_1_mem_read), .clr(Reset_Data_Memory_out));
  Multiplexer #(.width(32), .enable("false")) multiplexer_6 (
    .in0(alu_1_output), .in1(ram_1_data), .out(multiplexer_6_out), .sel(controller_1_mem_to_reg));

  // Notes on the sheet:
  //   contents of rom_1 (hex, n*v repeats v):
  //   f8400513 455593
endmodule

module Controller (
  input  [6:0] Opcode,
  output [2:0] ALUOP,
  output [1:0] Next_PC,
  output Operand_B,
  output [1:0] Operand_A,
  output [1:0] Extend_Sel,
  output Branch,
  output Mem_To_Reg,
  output Mem_Read,
  output Mem_Write,
  output Reg_Write
);

  wire Type_Controller_aui_pc, Type_Controller_i_type, Type_Controller_jalr, Type_Controller_load,
       Type_Controller_lui, Type_Controller_r_type, Type_Controller_s_type, Type_Controller_sb_type,
       Type_Controller_uj_type;

  Type_Control Type_Controller (
    .Opcode(Opcode), .R_Type(Type_Controller_r_type), .I_Type(Type_Controller_i_type),
    .Load(Type_Controller_load), .S_Type(Type_Controller_s_type), .SB_Type(Type_Controller_sb_type),
    .UJ_Type(Type_Controller_uj_type), .JALR(Type_Controller_jalr), .LUI(Type_Controller_lui),
    .AUI_PC(Type_Controller_aui_pc));
  Signal_Control Signal_Controller (
    .R_Type(Type_Controller_r_type), .I_Type(Type_Controller_i_type), .Load(Type_Controller_load),
    .S_Type(Type_Controller_s_type), .SB_Type(Type_Controller_sb_type), .UJ_Type(Type_Controller_uj_type),
    .JALR(Type_Controller_jalr), .LUI(Type_Controller_lui), .AUI_PC(Type_Controller_aui_pc),
    .Reg_Write(Reg_Write), .Mem_Write(Mem_Write), .Mem_Read(Mem_Read), .Mem_To_Reg(Mem_To_Reg),
    .Branch(Branch), .Extend_Select(Extend_Sel), .Operand_A(Operand_A), .Operand_B(Operand_B),
    .Next_PC(Next_PC), .ALU_Operation(ALUOP));
endmodule

module Signal_Control (
  input  R_Type,
  input  I_Type,
  input  Load,
  input  S_Type,
  input  SB_Type,
  input  UJ_Type,
  input  JALR,
  input  LUI,
  input  AUI_PC,
  output Reg_Write,
  output Mem_Write,
  output Mem_Read,
  output Mem_To_Reg,
  output Branch,
  output [1:0] Extend_Select,
  output [1:0] Operand_A,
  output Operand_B,
  output [1:0] Next_PC,
  output [2:0] ALU_Operation
);

  wire or_1_out, or_3_out;

  or or_1 (or_1_out, LUI, AUI_PC);
  or or_2 (Reg_Write, R_Type, I_Type, Load, UJ_Type, JALR, LUI);
  or or_3 (or_3_out, UJ_Type, JALR);
  or or_4 (Operand_B, Load, I_Type, AUI_PC, S_Type, LUI);
  ALUOP aluop_1 (
    .R_Type(R_Type), .I_Type(I_Type), .S_Type(S_Type), .SB_Type(SB_Type), .UJ_Type(UJ_Type), .JALR(JALR),
    .LUI(LUI), .Load(Load), .ALU_COntrol(ALU_Operation));
  _3I_to_2bitO u_3i_to_2bito_1 (._01(S_Type), ._10(or_1_out), .out_4(Extend_Select));  // open: _11
  _3I_to_2bitO u_3i_to_2bito_2 (._01(AUI_PC), ._11(LUI), ._10(or_3_out), .out_4(Operand_A));
  _3I_to_2bitO u_3i_to_2bito_3 (._01(UJ_Type), ._11(SB_Type), ._10(JALR), .out_4(Next_PC));

  assign Branch = SB_Type;
  assign Mem_Read = Load;
  assign Mem_To_Reg = Load;
  assign Mem_Write = S_Type;
endmodule

module Type_Control (
  input  [6:0] Opcode,
  output R_Type,
  output I_Type,
  output Load,
  output S_Type,
  output SB_Type,
  output UJ_Type,
  output JALR,
  output LUI,
  output AUI_PC
);

  Comparator #(.width(7), .mode("unsigned")) comparator_1 (.a(Opcode), .b(7'b0110011), .eq(R_Type));  // open: gt, lt
  Comparator #(.width(7), .mode("unsigned")) comparator_2 (.a(Opcode), .b(7'b0010011), .eq(I_Type));  // open: gt, lt
  Comparator #(.width(7), .mode("unsigned")) comparator_3 (.a(Opcode), .b(7'b0000011), .eq(Load));  // open: gt, lt
  Comparator #(.width(7), .mode("unsigned")) comparator_4 (.a(Opcode), .b(7'b0100011), .eq(S_Type));  // open: gt, lt
  Comparator #(.width(7), .mode("unsigned")) comparator_5 (.a(Opcode), .b(7'b1100011), .eq(SB_Type));  // open: gt, lt
  Comparator #(.width(7), .mode("unsigned")) comparator_6 (.a(Opcode), .b(7'b1101111), .eq(UJ_Type));  // open: gt, lt
  Comparator #(.width(7), .mode("unsigned")) comparator_7 (.a(Opcode), .b(7'b1100111), .eq(JALR));  // open: gt, lt
  Comparator #(.width(7), .mode("unsigned")) comparator_8 (.a(Opcode), .b(7'b0110111), .eq(LUI));  // open: gt, lt
  Comparator #(.width(7), .mode("unsigned")) comparator_9 (.a(Opcode), .b(7'b0010111), .eq(AUI_PC));  // open: gt, lt
endmodule

module _3I_to_2bitO (
  input  _01,
  input  _11,
  input  _10,
  output [1:0] out_4
);

  or or_1 (out_4[0], _01, _11);
  or or_2 (out_4[1], _11, _10);
endmodule

module ALUOP (
  input  R_Type,
  input  I_Type,
  input  S_Type,
  input  SB_Type,
  input  UJ_Type,
  input  JALR,
  input  LUI,
  input  Load,
  output [2:0] ALU_COntrol
);

  wire not_1_out, not_2_out, not_3_out, not_4_out, not_5_out, not_6_out, not_7_out, not_8_out, not_9_out,
       not_10_out, not_11_out, not_12_out, not_13_out;

  not not_1 (not_1_out, R_Type);
  not not_2 (not_2_out, SB_Type);
  not not_3 (not_3_out, LUI);
  not not_4 (not_4_out, Load);
  not not_5 (not_5_out, R_Type);
  not not_6 (not_6_out, I_Type);
  not not_7 (not_7_out, S_Type);
  not not_8 (not_8_out, Load);
  not not_9 (not_9_out, R_Type);
  not not_10 (not_10_out, I_Type);
  not not_11 (not_11_out, SB_Type);
  not not_12 (not_12_out, UJ_Type);
  not not_13 (not_13_out, JALR);
  and and_1 (ALU_COntrol[0], not_1_out, not_2_out, not_3_out, not_4_out);
  and and_2 (ALU_COntrol[1], not_5_out, not_6_out, not_7_out, not_8_out);
  and and_3 (ALU_COntrol[2], not_9_out, not_10_out, not_11_out, not_12_out, not_13_out);
endmodule

module Test (
  input  in_1,
  input  in_2,
  input  in_3,
  output [2:0] out_4
);

  Priority_Encoder priority_encoder_1 (
    .in0(in_1), .in3(in_2), .in4(in_3), .out(out_4));  // open: in1, in2, in5, in6, in7, en_in, gs, en_out
endmodule

module ALUController (
  input  [2:0] ALUOP,
  input  f7,
  input  [2:0] f3,
  output [4:0] out_4
);

  wire and_1_out, and_2_out, and_3_out, and_4_out, and_5_out, and_6_out, and_7_out, and_8_out, and_9_out,
       not_1_out, not_2_out, not_3_out, not_4_out, not_5_out, not_6_out, not_7_out, not_8_out, not_9_out,
       not_10_out, not_11_out, not_12_out, not_13_out, not_14_out, not_15_out, not_16_out, not_17_out,
       not_18_out, not_19_out, not_20_out, not_21_out, not_22_out, not_23_out;
  wire [2:0] priority_encoder_1_out;

  not not_1 (not_1_out, ALUOP[1]);
  not not_2 (not_2_out, ALUOP[2]);
  and and_1 (and_1_out, ALUOP[0], not_1_out, not_2_out);
  not not_3 (not_3_out, f3[1]);
  not not_4 (not_4_out, ALUOP[2]);
  not not_5 (not_5_out, ALUOP[0]);
  not not_6 (not_6_out, ALUOP[2]);
  not not_7 (not_7_out, ALUOP[0]);
  not not_8 (not_8_out, ALUOP[1]);
  not not_9 (not_9_out, ALUOP[2]);
  not not_10 (not_10_out, f7);
  not not_11 (not_11_out, ALUOP[0]);
  not not_12 (not_12_out, ALUOP[1]);
  not not_13 (not_13_out, ALUOP[2]);
  not not_14 (not_14_out, f7);
  not not_15 (not_15_out, ALUOP[1]);
  not not_16 (not_16_out, ALUOP[2]);
  and and_2 (and_2_out, f3[0], not_3_out, f3[2]);
  and and_3 (and_3_out, ALUOP[0], ALUOP[1], not_4_out);
  and and_4 (and_4_out, not_5_out, ALUOP[1], not_6_out);
  and and_5 (and_5_out, not_7_out, not_8_out, not_9_out, not_10_out);
  and and_6 (and_6_out, not_11_out, not_12_out, not_13_out, f7);
  and and_7 (and_7_out, not_14_out, ALUOP[0], not_15_out, not_16_out);
  and and_8 (and_8_out, f7, and_1_out, and_2_out);
  not not_17 (not_17_out, and_3_out);
  not not_18 (not_18_out, and_4_out);
  not not_19 (not_19_out, and_5_out);
  not not_20 (not_20_out, and_8_out);
  not not_21 (not_21_out, and_6_out);
  not not_22 (not_22_out, and_7_out);
  not not_23 (not_23_out, and_1_out);
  and and_9 (and_9_out, not_17_out, not_18_out, not_19_out, not_20_out, not_21_out, not_22_out, not_23_out);
  Priority_Encoder priority_encoder_1 (
    .in0(and_3_out), .in1(and_4_out), .in2(and_5_out), .in3(and_6_out), .in4(and_7_out), .in5(and_1_out),
    .in6(and_8_out), .in7(and_9_out), .out(priority_encoder_1_out));  // open: en_in, gs, en_out
  Multiplexer #(.select(3), .width(5), .enable("false")) multiplexer_1 (
    .in0({5{1'b1}}), .in1({2'b10, f3}), .in2({2'b00, f3}), .in3({2'b01, f3}), .in4({2'b00, f3}),
    .in5({2'b00, f3}), .in6({2'b01, f3}), .in7({5{1'b0}}), .out(out_4), .sel(priority_encoder_1_out));

  // Notes on the sheet:
  //   I Type
  //   JAL, JALR
  //   Branch
  //   R Type ( f7 = 0 )
  //   R Type ( f7 = 1 )
endmodule

module ALU (
  input  [31:0] Operand_A,
  input  [31:0] Operand_B,
  input  [4:0] ALUOperation,
  output [31:0] Output,
  output Branch
);

  wire comparator_1_eq, comparator_1_gt, comparator_1_lt, comparator_2_eq, comparator_2_gt, comparator_2_lt,
       comparator_3_eq, not_1_out, or_2_out, or_3_out;
  wire [31:0] adder_1_out, and_1_out, bit_extender_1_out, bit_extender_2_out, bit_extender_3_out,
       bit_extender_4_out, bit_extender_5_out, bit_extender_6_out, or_1_out, shifter_1_out, shifter_2_out,
       shifter_3_out, subtractor_1_out, xor_1_out;

  Comparator #(.width(32)) comparator_1 (
    .a(Operand_A), .b(Operand_B), .gt(comparator_1_gt), .eq(comparator_1_eq), .lt(comparator_1_lt));
  Comparator #(.width(32), .mode("unsigned")) comparator_2 (
    .a(Operand_A), .b(Operand_B), .gt(comparator_2_gt), .eq(comparator_2_eq), .lt(comparator_2_lt));
  Adder #(.width(32)) adder_1 (.a(Operand_A), .b(Operand_B), .out(adder_1_out));  // open: cin, cout
  Shifter #(.width(32)) shifter_1 (.in(Operand_A), .\dist (Operand_B[4:0]), .out(shifter_1_out));
  assign bit_extender_1_out = {{31{1'b0}}, comparator_1_lt};  // Bit_Extender bit_extender_1
  assign bit_extender_2_out = {{31{1'b0}}, comparator_2_lt};  // Bit_Extender bit_extender_2
  assign xor_1_out = Operand_A ^ Operand_B;  // XOR_Gate xor_1, 32 bits wide
  Shifter #(.width(32), .shift("lr")) shifter_2 (.in(Operand_A), .\dist (Operand_B[4:0]), .out(shifter_2_out));
  assign or_1_out = Operand_A | Operand_B;  // OR_Gate or_1, 32 bits wide
  assign and_1_out = Operand_A & Operand_B;  // AND_Gate and_1, 32 bits wide
  Subtractor #(.width(32)) subtractor_1 (.a(Operand_A), .b(Operand_B), .out(subtractor_1_out));  // open: bin, bout
  Shifter #(.width(32), .shift("ar")) shifter_3 (.in(Operand_A), .\dist (Operand_B[4:0]), .out(shifter_3_out));
  assign bit_extender_3_out = {{31{1'b0}}, comparator_1_eq};  // Bit_Extender bit_extender_3
  not not_1 (not_1_out, comparator_1_eq);
  assign bit_extender_4_out = {{31{1'b0}}, not_1_out};  // Bit_Extender bit_extender_4
  assign bit_extender_5_out = {{31{1'b0}}, or_2_out};  // Bit_Extender bit_extender_5
  or or_2 (or_2_out, comparator_1_eq, comparator_1_gt);
  assign bit_extender_6_out = {{31{1'b0}}, or_3_out};  // Bit_Extender bit_extender_6
  or or_3 (or_3_out, comparator_2_eq, comparator_2_gt);
  Multiplexer #(.select(5), .width(32), .enable("false")) multiplexer_1 (
    .in0(adder_1_out), .in1(shifter_1_out), .in2(bit_extender_1_out), .in3(bit_extender_2_out),
    .in4(xor_1_out), .in5(shifter_2_out), .in6(or_1_out), .in7(and_1_out), .in8(subtractor_1_out),
    .in13(shifter_3_out), .in16(bit_extender_3_out), .in17(bit_extender_4_out), .in20(bit_extender_1_out),
    .in21(bit_extender_5_out), .in22(bit_extender_2_out), .in23(bit_extender_6_out), .in31(Operand_A),
    .out(Output), .sel(ALUOperation));  // open: in9, in10, in11, in12, in14, in15, in18, in19, in24, in25, in26, in27, in28, in29, in30
  Comparator #(.width(32), .mode("unsigned")) comparator_3 (
    .a(Output), .b(32'h1), .eq(comparator_3_eq));  // open: gt, lt
  and and_2 (Branch, comparator_3_eq, ALUOperation[4]);

  // Notes on the sheet:
  //   OR
  //   AND
  //   ADD, ADDI
  //   SLL, SLLI
  //   SLT, SLTI, BLT
  //   SLTU, STLUI, BLTU
  //   XOR, XORI
  //   SRL, SRLI
  //   SUB
  //   SRA,SRAI
  //   BEQ
  //   BNE
  //   BGE
  //   BGEU
  //   COPY_A
endmodule

module Adder_for_JALR (
  input  [31:0] RS1,
  input  [31:0] IMM,
  output [31:0] Computed_Address
);

  wire [31:0] adder_1_out;

  Adder #(.width(32)) adder_1 (.a(RS1), .b(IMM), .out(adder_1_out));  // open: cin, cout
  assign Computed_Address = adder_1_out & 32'hfffffffe;  // AND_Gate and_1, 32 bits wide
endmodule
